# Fritzing sketch fritzing (saved by Fritzing 0.9.3b)
circuit board: 11cm x 6cm

parts:
  MCU1 = Raspberry Pi Zero
  Teensy_3_1 = Teensy 3.1
  OP27a = OP37 - Low Noise, Precision, High Speed Op Amp [part_number=OP37]
  R1 = Resistor [tolerance=±5% resistance=8.2k package=THT]
  R2 = Resistor [tolerance=±5% resistance=3.9k package=THT]
  OP27b = OP37 - Low Noise, Precision, High Speed Op Amp [part_number=OP37]
  R3 = Resistor [tolerance=±5% resistance=1k package=THT]
  C4 = Ceramic Capacitor [capacitance=4.7nF package="100 mil [THT, multilayer]"]
  R4 = Resistor [tolerance=±5% resistance=16k package=THT]
  C5 = Ceramic Capacitor [capacitance=470pF package="100 mil [THT, multilayer]"]
  C6 = Ceramic Capacitor [capacitance=470pF package="100 mil [THT, multilayer]"]
  Comp = Dual Op-Amp [package=dip08]
  R5 = Resistor [tolerance=±5% resistance=1k package=THT]
  R6 = Resistor [tolerance=±5% resistance=1k package=THT]
  R7 = Resistor [tolerance=±5% resistance=1k package=THT]
  R8 = Resistor [tolerance=±5% resistance=1.6k package=THT]
  R9 = Resistor [tolerance=±5% resistance=16k package=THT]
  C9 = Ceramic Capacitor [capacitance=10nF package="100 mil [THT, multilayer]"]
  C7 = Ceramic Capacitor [capacitance=10nF package="100 mil [THT, multilayer]"]
  XOR = 4786 4 x 2 Input XOR Gate, multi-part [part_number=4786 package="DIP (Dual Inline) [THT]"]
  Part1 = 4786 4 x 2 Input XOR Gate, multi-part [part_number=4786 package="DIP (Dual Inline) [THT]"]
  XOR_1 = 4786 4 x 2 Input XOR Gate, multi-part [part_number=4786 package="DIP (Dual Inline) [THT]"]
  XOR_2 = 4786 4 x 2 Input XOR Gate, multi-part [part_number=4786 package="DIP (Dual Inline) [THT]"]
  XOR_3 = 4786 4 x 2 Input XOR Gate, multi-part [part_number=4786 package="DIP (Dual Inline) [THT]"]  # not connected
  XOR_4 = 4786 4 x 2 Input XOR Gate, multi-part [part_number=4786 package="DIP (Dual Inline) [THT]"]  # not connected
  R10 = Resistor [tolerance=±5% resistance=16k package=THT]
  R11 = Resistor [tolerance=±5% resistance=1.6k package=THT]
  R12 = Resistor [tolerance=±5% resistance=1k package=THT]
  C10 = Ceramic Capacitor [capacitance=10nF package="100 mil [THT, multilayer]"]
  C11 = Ceramic Capacitor [capacitance=10nF package="100 mil [THT, multilayer]"]
  Transmitter = Piezo Speaker
  Receiver = Piezo Speaker
  C1 = Capacitor Polarized [package=cpol-radial-10uf-25v]
  C12 = Ceramic Capacitor [capacitance=10nF package="100 mil [THT, multilayer]"]
  C13 = Ceramic Capacitor [capacitance=10nF package="100 mil [THT, multilayer]"]

nets:
  N1: MCU1.pin_4, Teensy_3_1.3V3
  GND: MCU1.pin_6, MCU1.pin_34, Teensy_3_1.GND, OP27a.-V, R2.Pin_1, OP27b.-V, Comp.A_V-, R8.Pin_1, C9.1, C7.0, XOR.connector6, Part1.GND, R11.Pin_1, C10.0, C11.1, Transmitter.pin1, Receiver.pin1, C1.-, C12.0, C13.0
  N2: MCU1.pin_8, Teensy_3_1.D0
  N3: MCU1.pin_10, Teensy_3_1.D1
  N4: Teensy_3_1.D5, XOR.connector3, XOR_2.A2
  N5: Teensy_3_1.D6, XOR.connector0, XOR_1.A1
  N6: Teensy_3_1.A0/D14, R10.Pin_1, C10.1, C11.0
  N7: Teensy_3_1.A1/D15, R9.Pin_1, C9.0, C7.1
  N8: Teensy_3_1.A9/D23, Transmitter.pin2
  VIN: Teensy_3_1.Vin, OP27a.V+, R1.Pin_0, OP27b.V+, Comp.A_V+, R5.Pin_0, R6.Pin_0, XOR.connector13, Part1.VDD, C1.+, C12.1, C13.1
  N9: OP27a.-IN, OP27a.OUT, OP27b.+IN, Comp.A_-IN, Comp.B_-IN
  N10: OP27a.+IN, R1.Pin_1, R2.Pin_0
  N11: OP27b.-IN, R3.Pin_1, R4.Pin_0, C5.1
  N12: OP27b.OUT, R4.Pin_1, C6.0, Comp.A_+IN, Comp.B_+IN
  N13: R3.Pin_0, C4.0
  N14: C4.1, Receiver.pin2
  N15: C5.0, C6.1
  N16: Comp.A_OUT, R5.Pin_1, XOR.connector4, XOR_2.B2
  N17: Comp.B_OUT, R6.Pin_1, XOR.connector1, XOR_1.B1
  N18: R7.Pin_0, XOR.connector5, XOR_2.Q2
  N19: R7.Pin_1, R8.Pin_0, R9.Pin_0
  N20: XOR.connector2, XOR_1.Q1, R12.Pin_0
  N21: R10.Pin_0, R11.Pin_0, R12.Pin_1

custom parts:
  4786 4 x 2 Input XOR Gate, multi-part: 4786 4 x 2 Input XOR Gate with sub-parts
  4786 4 x 2 Input XOR Gate, multi-part: 4786 4 x 2 Input XOR Gate with sub-parts
  4786 4 x 2 Input XOR Gate, multi-part: 4786 4 x 2 Input XOR Gate with sub-parts
  4786 4 x 2 Input XOR Gate, multi-part: 4786 4 x 2 Input XOR Gate with sub-parts
  4786 4 x 2 Input XOR Gate, multi-part: 4786 4 x 2 Input XOR Gate with sub-parts
  4786 4 x 2 Input XOR Gate, multi-part: 4786 4 x 2 Input XOR Gate with sub-parts
